# Fritzing sketch ESQUEMÁTICO (FZZ) (saved by Fritzing 0.9.4)
breadboards: 4

parts:
  Componente1 = Arduino Nano (Rev3.0)
  R1 = Resistor [tolerance=±5% resistance=220 package=THT]
  R2 = Resistor [tolerance=±5% resistance=220 package=THT]
  R3 = Resistor [tolerance=±5% resistance=220 package=THT]
  R4 = Resistor [tolerance=±5% resistance=220 package=THT]
  LED1 = LED - 5mm [color="Red (633nm)" package="5 mm [THT]"]
  LED2 = LED - 5mm [color="Red (633nm)" package="5 mm [THT]"]
  LED3 = LED - 5mm [color="Red (633nm)" package="5 mm [THT]"]
  LED4 = LED - 5mm [color="Red (633nm)" package="5 mm [THT]"]
  S1 = Pushbutton [package=THT]
  S2 = Pushbutton [package=THT]
  R5 = Resistor [tolerance=±5% resistance=10k package=THT]
  R6 = Resistor [tolerance=±5% resistance=10k package=THT]
  Componente2 = Arduino Nano (Rev3.0)
  R7 = Resistor [tolerance=±5% resistance=220 package=THT]
  R8 = Resistor [tolerance=±5% resistance=220 package=THT]
  R9 = Resistor [tolerance=±5% resistance=220 package=THT]
  R10 = Resistor [tolerance=±5% resistance=220 package=THT]
  LED5 = LED - 5mm [color="Red (633nm)" package="5 mm [THT]"]
  LED6 = LED - 5mm [color="Red (633nm)" package="5 mm [THT]"]
  LED7 = LED - 5mm [color="Red (633nm)" package="5 mm [THT]"]
  LED8 = LED - 5mm [color="Red (633nm)" package="5 mm [THT]"]
  R11 = Resistor [tolerance=±5% resistance=10k package=THT]
  R12 = Resistor [tolerance=±5% resistance=10k package=THT]
  S3 = Pushbutton [package="[THT]"]
  S4 = Pushbutton [package="[THT]"]
  buz1 = Piezo Buzzer
  buz2 = Piezo Buzzer
  R13 = Resistor [tolerance=±5% resistance=220 package=THT]
  R14 = Resistor [tolerance=±5% resistance=220 package=THT]
  R15 = Resistor [tolerance=±5% resistance=220 package=THT]
  R16 = Resistor [tolerance=±5% resistance=220 package=THT]
  LED9 = LED - 5mm [color="Red (633nm)" package="5 mm [THT]"]
  LED10 = LED - 5mm [color="Red (633nm)" package="5 mm [THT]"]
  LED11 = LED - 5mm [color="Red (633nm)" package="5 mm [THT]"]
  LED12 = LED - 5mm [color="Red (633nm)" package="5 mm [THT]"]
  S5 = Pushbutton [package=THT]
  S6 = Pushbutton [package=THT]
  R17 = Resistor [tolerance=±5% resistance=10k package=THT]
  R18 = Resistor [tolerance=±5% resistance=10k package=THT]
  buz3 = Piezo Buzzer
  Componente3 = Arduino Uno (Rev3) - ICSP
  Componente4 = Arduino Uno (Rev3) - ICSP
  R19 = Resistor [tolerance=±5% resistance=220 package=THT]
  R20 = Resistor [tolerance=±5% resistance=220 package=THT]
  R21 = Resistor [tolerance=±5% resistance=220 package=THT]
  R22 = Resistor [tolerance=±5% resistance=220 package=THT]
  LED13 = LED - 5mm [color="Red (633nm)" package="5 mm [THT]"]
  LED14 = LED - 5mm [color="Red (633nm)" package="5 mm [THT]"]
  LED15 = LED - 5mm [color="Red (633nm)" package="5 mm [THT]"]
  LED16 = LED - 5mm [color="Red (633nm)" package="5 mm [THT]"]
  R23 = Resistor [tolerance=±5% resistance=10k package=THT]
  R24 = Resistor [tolerance=±5% resistance=10k package=THT]
  buz4 = Piezo Buzzer
  S7 = Pushbutton [package="[THT]"]
  S8 = Pushbutton [package="[THT]"]

nets:
  N1: Componente1.GND, LED1.cathode, LED2.cathode, LED3.cathode, LED4.cathode, R5.Pin_1, R6.Pin_1, buz1.pin_2
  N2: Componente1.D2, R1.Pin_0
  N3: Componente1.D3, R2.Pin_0
  N4: Componente1.D4, R3.Pin_0
  N5: Componente1.D5, R4.Pin_0
  N6: Componente1.D6, buz1.pin_1
  N7: Componente1.D7, S1.leg1, R5.Pin_0
  N8: Componente1.D8, S2.leg1, R6.Pin_0
  N9: Componente1.5V, S1.leg0, S2.leg0
  N10: R1.Pin_1, LED1.anode
  N11: R2.Pin_1, LED2.anode
  N12: R3.Pin_1, LED3.anode
  N13: R4.Pin_1, LED4.anode
  N14: Componente2.GND, LED5.cathode, LED6.cathode, LED7.cathode, LED8.cathode, R11.Pin_1, R12.Pin_1, buz2.pin_2
  N15: Componente2.D2, R7.Pin_0
  N16: Componente2.D3, R8.Pin_0
  N17: Componente2.D4, R9.Pin_0
  N18: Componente2.D5, R10.Pin_0
  N19: Componente2.D6, buz2.pin_1
  N20: Componente2.D7, R11.Pin_0, S3.Pin_3, S3.Pin_4
  N21: Componente2.D8, R12.Pin_0, S4.Pin_3, S4.Pin_4
  N22: Componente2.5V, S3.Pin_1, S3.Pin_2, S4.Pin_1, S4.Pin_2
  N23: R7.Pin_1, LED6.anode
  N24: R8.Pin_1, LED8.anode
  N25: R9.Pin_1, LED5.anode
  N26: R10.Pin_1, LED7.anode
  N27: R13.Pin_0, Componente3.D2
  N28: R13.Pin_1, LED12.anode
  N29: R14.Pin_0, Componente3.D3_PWM
  N30: R14.Pin_1, LED9.anode
  N31: R15.Pin_0, Componente3.D4
  N32: R15.Pin_1, LED11.anode
  N33: R16.Pin_0, Componente3.D5_PWM
  N34: R16.Pin_1, LED10.anode
  N35: LED9.cathode, LED10.cathode, LED11.cathode, LED12.cathode, R17.Pin_1, R18.Pin_1, buz3.pin_2, Componente3.GND
  N36: S5.leg0, S6.leg0, Componente3.5V
  N37: S5.leg1, R18.Pin_0, Componente3.D7
  N38: S6.leg1, R17.Pin_0, Componente3.D8
  N39: buz3.pin_1, Componente3.D6_PWM
  N40: Componente4.D8, R23.Pin_0, S8.Pin_1, S8.Pin_2
  N41: Componente4.D2, R19.Pin_0
  N42: Componente4.D3_PWM, R20.Pin_0
  N43: Componente4.D4, R21.Pin_0
  N44: Componente4.D5_PWM, R22.Pin_0
  N45: Componente4.D6_PWM, buz4.pin_1
  N46: Componente4.D7, R24.Pin_0, S7.Pin_1, S7.Pin_2
  N47: Componente4.5V, S7.Pin_3, S7.Pin_4, S8.Pin_3, S8.Pin_4
  N48: Componente4.GND, LED13.cathode, LED14.cathode, LED15.cathode, LED16.cathode, R23.Pin_1, R24.Pin_1, buz4.pin_2
  N49: R19.Pin_1, LED14.anode
  N50: R20.Pin_1, LED13.anode
  N51: R21.Pin_1, LED16.anode
  N52: R22.Pin_1, LED15.anode

notes:
  ARDUINO NANO: CIRCUITO CON LEDs, BUZZER Y BOTONES DE DOS TERMINALES
  ARDUINO NANO: CIRCUITO CON LEDs, BUZZER Y BOTONES DE CUATRO TERMINALES
  ARDUINO UNO: CIRCUITO CON LEDs, BUZZER Y BOTONES DE DOS TERMINALES
  ARDUINO UNO: CIRCUITO CON LEDs, BUZZER Y BOTONES DE CUATRO TERMINALES

custom parts:
  Piezo Buzzer: Part from https://www.nutsvolts.com/magazine/article/november2012_SmileysWorkshop modified to be .3 in spacing to match the adafruit buzzer 5V breadboard friendly part.
