# Fritzing sketch ESQUEMÁTICO (saved by Fritzing 0.9.4)
breadboards: 2

parts:
  Componente1 = Arduino Nano (Rev3.0)
  R1 = Rotary Potentiometer (Small) [maximum_resistance=100kΩ package=THT]
  R2 = Resistor [tolerance=±5% resistance=220 package=THT]
  LED1 = LED - 5mm [color="Red (633nm)" package="5 mm [THT]"]
  R3 = Resistor [tolerance=±5% resistance=220 package=THT]
  LED2 = LED - 5mm [color="Red (633nm)" package="5 mm [THT]"]
  R4 = Resistor [tolerance=±5% resistance=220 package=THT]
  R5 = Resistor [tolerance=±5% resistance=220 package=THT]
  LED3 = LED - 5mm [color="Red (633nm)" package="5 mm [THT]"]
  LED4 = LED - 5mm [color="Red (633nm)" package="5 mm [THT]"]
  R6 = Photocell (LDR) [package=THT]
  R7 = Resistor [tolerance=±5% resistance=10k package=THT]
  T1 = LM35 Temperature Sensor [package="TO92 [THT]"]
  R8 = Rotary Potentiometer (Small) [maximum_resistance=100kΩ package=THT]
  R9 = Resistor [tolerance=±5% resistance=220 package=THT]
  R10 = Resistor [tolerance=±5% resistance=220 package=THT]
  R11 = Resistor [tolerance=±5% resistance=220 package=THT]
  R12 = Resistor [tolerance=±5% resistance=220 package=THT]
  LED5 = LED - 5mm [color="Red (633nm)" package="5 mm [THT]"]
  LED6 = LED - 5mm [color="Red (633nm)" package="5 mm [THT]"]
  LED7 = LED - 5mm [color="Red (633nm)" package="5 mm [THT]"]
  LED8 = LED - 5mm [color="Red (633nm)" package="5 mm [THT]"]
  R13 = Photocell (LDR) [package=THT]
  R14 = Resistor [tolerance=±5% resistance=10k package=THT]
  T2 = LM35 Temperature Sensor [package="TO92 [THT]"]
  Componente2 = Arduino Uno (Rev3)

nets:
  GND: Componente1.GND, R1.leg1, R2.Pin_1, R3.Pin_1, R4.Pin_1, R5.Pin_1, R7.Pin_1, T1.GND
  N1: Componente1.D2, LED1.cathode
  N2: Componente1.D3, LED2.cathode
  N3: Componente1.D4, LED3.cathode
  N4: Componente1.D5, LED4.cathode
  N5: Componente1.5V, R1.leg2, R6.pin_1, T1.+Vs
  N6: Componente1.A2, T1.Vout
  N7: Componente1.A1, R6.pin_0, R7.Pin_0
  N8: Componente1.A0, R1.wiper
  N9: R2.Pin_0, LED1.anode
  N10: R3.Pin_0, LED2.anode
  N11: R4.Pin_0, LED4.anode
  N12: R5.Pin_0, LED3.anode
  GND_2: R8.leg1, R9.Pin_1, R10.Pin_1, R11.Pin_1, R12.Pin_1, R14.Pin_1, T2.GND, Componente2.GND
  N13: R8.wiper, Componente2.A0
  N14: R8.leg2, R13.pin_1, T2.+Vs, Componente2.5V
  N15: R9.Pin_0, LED8.anode
  N16: R10.Pin_0, LED5.anode
  N17: R11.Pin_0, LED7.anode
  N18: R12.Pin_0, LED6.anode
  N19: LED5.cathode, Componente2.D5_PWM
  N20: LED6.cathode, Componente2.D3_PWM
  N21: LED7.cathode, Componente2.D4
  N22: LED8.cathode, Componente2.D2
  N23: R13.pin_0, R14.Pin_0, Componente2.A1
  N24: T2.Vout, Componente2.A2
