# Fritzing sketch ESQUEMÁTICO (FZZ) (saved by Fritzing 0.9.4)
breadboards: 6

parts:
  Componente1 = Arduino Nano (Rev3.0)
  HC-SR04_Sensor_1 = HC-SR04 Ultrasonic Distance Sensor
  R1 = Resistor [tolerance=±5% resistance=220 package=THT]
  R2 = Resistor [tolerance=±5% resistance=220 package=THT]
  R3 = Resistor [tolerance=±5% resistance=220 package=THT]
  R4 = Resistor [tolerance=±5% resistance=220 package=THT]
  LED1 = LED - 5mm [color="Red (633nm)" package="5 mm [THT]"]
  LED2 = LED - 5mm [color="Red (633nm)" package="5 mm [THT]"]
  LED3 = LED - 5mm [color="Red (633nm)" package="5 mm [THT]"]
  LED4 = LED - 5mm [color="Red (633nm)" package="5 mm [THT]"]
  buz1 = Piezo Buzzer
  Componente2 = Arduino Nano (Rev3.0)
  LED5 = RGB LED (com. cathode, rgb) [package="5 mm [THT]"]
  R5 = Resistor [tolerance=±5% resistance=220 package=THT]
  R6 = Resistor [tolerance=±5% resistance=10k package=THT]
  S1 = Pushbutton [package="[THT]"]
  R7 = Rotary Potentiometer (Small) [maximum_resistance=100kΩ package=THT]
  Componente3 = Arduino Nano (Rev3.0)
  LED6 = RGB LED (com. cathode, rgb) [package="5 mm [THT]"]
  R8 = Resistor [tolerance=±5% resistance=220 package=THT]
  R9 = Resistor [tolerance=±5% resistance=10k package=THT]
  S2 = Pushbutton [package="[THT]"]
  R10 = Rotary Potentiometer (Small) [maximum_resistance=100kΩ package=THT]
  HC-SR04_Sensor_2 = HC-SR04 Ultrasonic Distance Sensor
  R11 = Resistor [tolerance=±5% resistance=220 package=THT]
  R12 = Resistor [tolerance=±5% resistance=220 package=THT]
  R13 = Resistor [tolerance=±5% resistance=220 package=THT]
  R14 = Resistor [tolerance=±5% resistance=220 package=THT]
  LED7 = LED - 5mm [color="Red (633nm)" package="5 mm [THT]"]
  LED8 = LED - 5mm [color="Red (633nm)" package="5 mm [THT]"]
  LED9 = LED - 5mm [color="Red (633nm)" package="5 mm [THT]"]
  LED10 = LED - 5mm [color="Red (633nm)" package="5 mm [THT]"]
  buz2 = Piezo Buzzer
  Componente4 = Arduino Uno (Rev3)
  LED11 = RGB LED (com. cathode, rgb) [package="5 mm [THT]"]
  R15 = Resistor [tolerance=±5% resistance=220 package=THT]
  R16 = Resistor [tolerance=±5% resistance=10k package=THT]
  S3 = Pushbutton [package="[THT]"]
  R17 = Rotary Potentiometer (Small) [maximum_resistance=100kΩ package=THT]
  Componente5 = Arduino Uno (Rev3)
  Componente6 = Arduino Uno (Rev3)
  LED12 = RGB LED (com. cathode, rgb) [package="5 mm [THT]"]
  R18 = Resistor [tolerance=±5% resistance=220 package=THT]
  R19 = Resistor [tolerance=±5% resistance=10k package=THT]
  S4 = Pushbutton [package="[THT]"]
  R20 = Rotary Potentiometer (Small) [maximum_resistance=100kΩ package=THT]
  LED13 = RGB LED (com. cathode, rgb) [package="5 mm [THT]"]
  R21 = Resistor [tolerance=±5% resistance=220 package=THT]
  LED14 = RGB LED (com. cathode, rgb) [package="5 mm [THT]"]
  R22 = Resistor [tolerance=±5% resistance=220 package=THT]

nets:
  GND: Componente1.GND, HC-SR04_Sensor_1.GND, R1.Pin_1, R2.Pin_1, R3.Pin_1, R4.Pin_1, buz1.pin_2
  N1: Componente1.D2, LED1.anode
  N2: Componente1.D3, LED2.anode
  N3: Componente1.D4, LED3.anode
  N4: Componente1.D5, LED4.anode
  N5: Componente1.D6, buz1.pin_1
  N6: Componente1.D7, HC-SR04_Sensor_1.TRIG
  N7: Componente1.D8, HC-SR04_Sensor_1.ECHO
  5V: Componente1.5V, HC-SR04_Sensor_1.VCC
  N8: R1.Pin_0, LED4.cathode
  N9: R2.Pin_0, LED3.cathode
  N10: R3.Pin_0, LED2.cathode
  N11: R4.Pin_0, LED1.cathode
  N12: Componente2.GND, R5.Pin_1, R6.Pin_1, R7.leg1
  N13: Componente2.D8, R6.Pin_0, S1.Pin_3, S1.Pin_4
  N14: Componente2.D9, LED5.blue_anode
  N15: Componente2.D10, LED5.green_anode
  N16: Componente2.D11/MOSI, LED5.red_anode
  N17: Componente2.5V, S1.Pin_1, S1.Pin_2, R7.leg2
  N18: Componente2.A0, R7.wiper
  N19: LED5.common_cathode, R5.Pin_0
  N20: Componente3.GND, R9.Pin_1, R10.leg1, R21.Pin_1, LED14.red_anode
  N21: Componente3.D8, R9.Pin_0, S2.Pin_3, S2.Pin_4
  N22: Componente3.D9, LED6.blue_anode
  N23: Componente3.D10, LED6.green_anode
  N24: Componente3.D11/MOSI, LED6.red_anode
  N25: Componente3.5V, R8.Pin_1, S2.Pin_1, S2.Pin_2, R10.leg2, LED13.red_anode, R22.Pin_1
  N26: Componente3.A0, R10.wiper
  N27: LED6.common_cathode, R8.Pin_0
  VCC: HC-SR04_Sensor_2.VCC, Componente4.5V
  N28: HC-SR04_Sensor_2.TRIG, Componente4.D7
  N29: HC-SR04_Sensor_2.ECHO, Componente4.D8
  GND_2: HC-SR04_Sensor_2.GND, R11.Pin_1, R12.Pin_1, R13.Pin_1, R14.Pin_1, buz2.pin_2, Componente4.GND
  N30: R11.Pin_0, LED10.cathode
  N31: R12.Pin_0, LED9.cathode
  N32: R13.Pin_0, LED8.cathode
  N33: R14.Pin_0, LED7.cathode
  N34: LED7.anode, Componente4.D2
  N35: LED8.anode, Componente4.D3_PWM
  N36: LED9.anode, Componente4.D4
  N37: LED10.anode, Componente4.D5_PWM
  N38: buz2.pin_1, Componente4.D6_PWM
  N39: LED11.red_anode, Componente5.D11_PWM/MOSI
  N40: LED11.common_cathode, R15.Pin_0
  N41: LED11.green_anode, Componente5.D10_PWM/SS
  N42: LED11.blue_anode, Componente5.D9_PWM
  N43: R15.Pin_1, R16.Pin_1, R17.leg1, Componente5.GND
  N44: R16.Pin_0, S3.Pin_3, S3.Pin_4, Componente5.D8
  N45: S3.Pin_1, S3.Pin_2, R17.leg2, Componente5.5V
  N46: R17.wiper, Componente5.A0
  N47: Componente6.A0, R20.wiper
  N48: Componente6.D8, R19.Pin_0, S4.Pin_3, S4.Pin_4
  N49: Componente6.D9_PWM, LED12.blue_anode
  N50: Componente6.D10_PWM/SS, LED12.green_anode
  N51: Componente6.D11_PWM/MOSI, LED12.red_anode
  N52: Componente6.5V, R18.Pin_1, S4.Pin_1, S4.Pin_2, R20.leg2
  N53: Componente6.GND, R19.Pin_1, R20.leg1
  N54: LED12.common_cathode, R18.Pin_0
  N55: LED13.common_cathode, R21.Pin_0
  N56: LED14.common_cathode, R22.Pin_0

notes:
  Circuito de configuración HC-SR04
  Conexión para LED RGB (Cátodo Común)
  Conexión para LED RGB (Ánodo Común)

custom parts:
  Piezo Buzzer: Part from https://www.nutsvolts.com/magazine/article/november2012_SmileysWorkshop modified to be .3 in spacing to match the adafruit buzzer 5V breadboard friendly part.
