# Fritzing sketch ESQUEMÁTICOS_FZZ (saved by Fritzing 0.9.4)
breadboards: 5

parts:
  U1 = 74HC595 [package="DIP16 [THT]"]
  U2 = 74HC595 [package="DIP16 [THT]"]
  Componente1 = Arduino Nano (Rev3.0)
  7_Segment3 = 7 Segment Display
  7_Segment4 = 7 Segment Display
  R5 = Resistor [tolerance=±5% resistance=220 package=THT]
  R6 = Resistor [tolerance=±5% resistance=220 package=THT]
  R7 = Resistor [tolerance=±5% resistance=220 package=THT]
  R8 = Resistor [tolerance=±5% resistance=220 package=THT]
  U3 = 74HC595 [package="DIP16 [THT]"]
  U4 = 74HC595 [package="DIP16 [THT]"]
  Componente2 = Arduino Nano (Rev3.0)
  7_Segment5 = 7 Segment Display
  7_Segment6 = 7 Segment Display
  R9 = Resistor [tolerance=±5% resistance=220 package=THT]
  R10 = Resistor [tolerance=±5% resistance=220 package=THT]
  R11 = Resistor [tolerance=±5% resistance=220 package=THT]
  R12 = Resistor [tolerance=±5% resistance=220 package=THT]
  U5 = 74HC595 [package="DIP16 [THT]"]
  U6 = 74HC595 [package="DIP16 [THT]"]
  7_Segment7 = 7 Segment Display
  7_Segment8 = 7 Segment Display
  R13 = Resistor [tolerance=±5% resistance=220 package=THT]
  R14 = Resistor [tolerance=±5% resistance=220 package=THT]
  R15 = Resistor [tolerance=±5% resistance=220 package=THT]
  R16 = Resistor [tolerance=±5% resistance=220 package=THT]
  Componente3 = Arduino Uno (Rev3)
  Componente4 = Arduino Uno (Rev3)
  U7 = 74HC595 [package="DIP16 [THT]"]
  U8 = 74HC595 [package="DIP16 [THT]"]
  7_Segment9 = 7 Segment Display
  7_Segment10 = 7 Segment Display
  R17 = Resistor [tolerance=±5% resistance=220 package=THT]
  R18 = Resistor [tolerance=±5% resistance=220 package=THT]
  R19 = Resistor [tolerance=±5% resistance=220 package=THT]
  R20 = Resistor [tolerance=±5% resistance=220 package=THT]
  7_Segment11 = 7 Segment Display
  7_Segment12 = 7 Segment Display
  R21 = Resistor [tolerance=±5% resistance=220 package=THT]
  R22 = Resistor [tolerance=±5% resistance=220 package=THT]
  Componente5 = Arduino Uno (Rev3)

nets:
  N1: U1.Q1, 7_Segment4.Segment_A
  N2: U1.Q2, 7_Segment4.Segment_B
  N3: U1.Q3, 7_Segment4.Segment_C
  N4: U1.Q4, 7_Segment4.Segment_D
  N5: U1.Q5, 7_Segment4.Segment_E
  N6: U1.Q6, 7_Segment4.Segment_F
  N7: U1.Q7, 7_Segment4.Segment_G
  GND: U1.GND, U1.OE, U2.GND, U2.OE, Componente1.GND, R5.Pin_0, R6.Pin_1, R7.Pin_0, R8.Pin_1
  VCC: U1.MR, U1.VCC, U2.MR, U2.VCC, Componente1.5V
  N8: U1.SH_CP, U2.SH_CP, Componente1.D4
  N9: U1.ST_CP, U2.ST_CP, Componente1.D3
  N10: U1.DS, U2.Q7'
  N11: U2.Q1, 7_Segment3.Segment_A
  N12: U2.Q2, 7_Segment3.Segment_B
  N13: U2.Q3, 7_Segment3.Segment_C
  N14: U2.Q4, 7_Segment3.Segment_D
  N15: U2.Q5, 7_Segment3.Segment_E
  N16: U2.Q6, 7_Segment3.Segment_F
  N17: U2.Q7, 7_Segment3.Segment_G
  N18: U2.DS, Componente1.D2
  N19: 7_Segment3.common_cathode, R5.Pin_1, R6.Pin_0
  N20: 7_Segment4.common_cathode, R7.Pin_1, R8.Pin_0
  N21: U3.Q1, 7_Segment5.Segment_A
  N22: U3.Q2, 7_Segment5.Segment_B
  N23: U3.Q3, 7_Segment5.Segment_C
  N24: U3.Q4, 7_Segment5.Segment_D
  N25: U3.Q5, 7_Segment5.Segment_E
  N26: U3.Q6, 7_Segment5.Segment_F
  N27: U3.Q7, 7_Segment5.Segment_G
  GND_2: U3.GND, U3.OE, U4.GND, U4.OE, Componente2.GND
  N28: U3.Q7', U4.DS
  VCC_2: U3.MR, U3.VCC, U4.MR, U4.VCC, Componente2.5V, R9.Pin_0, R10.Pin_0, R11.Pin_1, R12.Pin_1
  N29: U3.SH_CP, U4.SH_CP, Componente2.D4
  N30: U3.ST_CP, U4.ST_CP, Componente2.D3
  N31: U3.DS, Componente2.D2
  N32: U4.Q1, 7_Segment6.Segment_A
  N33: U4.Q2, 7_Segment6.Segment_B
  N34: U4.Q3, 7_Segment6.Segment_C
  N35: U4.Q4, 7_Segment6.Segment_D
  N36: U4.Q5, 7_Segment6.Segment_E
  N37: U4.Q6, 7_Segment6.Segment_F
  N38: U4.Q7, 7_Segment6.Segment_G
  N39: 7_Segment5.common_cathode, R9.Pin_1, R12.Pin_0
  N40: 7_Segment6.common_cathode, R10.Pin_1, R11.Pin_0
  N41: U5.Q1, 7_Segment7.Segment_A
  N42: U5.Q2, 7_Segment7.Segment_B
  N43: U5.Q3, 7_Segment7.Segment_C
  N44: U5.Q4, 7_Segment7.Segment_D
  N45: U5.Q5, 7_Segment7.Segment_E
  N46: U5.Q6, 7_Segment7.Segment_F
  N47: U5.Q7, 7_Segment7.Segment_G
  GND_3: U5.GND, U5.OE, U6.GND, U6.OE, R13.Pin_0, R14.Pin_1, R15.Pin_1, R16.Pin_0, Componente3.GND
  N48: U5.Q7', U6.DS
  VCC_3: U5.MR, U5.VCC, U6.MR, U6.VCC, Componente3.5V
  N49: U5.SH_CP, U6.SH_CP, Componente3.D4
  N50: U5.ST_CP, U6.ST_CP, Componente3.D3_PWM
  N51: U5.DS, Componente3.D2
  N52: U6.Q1, 7_Segment8.Segment_A
  N53: U6.Q2, 7_Segment8.Segment_B
  N54: U6.Q3, 7_Segment8.Segment_C
  N55: U6.Q4, 7_Segment8.Segment_D
  N56: U6.Q5, 7_Segment8.Segment_E
  N57: U6.Q6, 7_Segment8.Segment_F
  N58: U6.Q7, 7_Segment8.Segment_G
  N59: 7_Segment7.common_cathode, R13.Pin_1, R14.Pin_0
  N60: 7_Segment8.common_cathode, R15.Pin_0, R16.Pin_1
  N61: Componente4.D2, U7.DS
  N62: Componente4.D3_PWM, U7.ST_CP, U8.ST_CP
  N63: Componente4.D4, U7.SH_CP, U8.SH_CP
  VCC_4: Componente4.5V, U7.MR, U7.VCC, U8.MR, U8.VCC
  GND_4: Componente4.GND, U7.GND, U7.OE, U8.GND, U8.OE, R17.Pin_1, R18.Pin_1, R19.Pin_0, R20.Pin_0
  N64: U7.Q1, 7_Segment10.Segment_A
  N65: U7.Q2, 7_Segment10.Segment_B
  N66: U7.Q3, 7_Segment10.Segment_C
  N67: U7.Q4, 7_Segment10.Segment_D
  N68: U7.Q5, 7_Segment10.Segment_E
  N69: U7.Q6, 7_Segment10.Segment_F
  N70: U7.Q7, 7_Segment10.Segment_G
  N71: U7.Q7', U8.DS
  N72: U8.Q1, 7_Segment9.Segment_A
  N73: U8.Q2, 7_Segment9.Segment_B
  N74: U8.Q3, 7_Segment9.Segment_C
  N75: U8.Q4, 7_Segment9.Segment_D
  N76: U8.Q5, 7_Segment9.Segment_E
  N77: U8.Q6, 7_Segment9.Segment_F
  N78: U8.Q7, 7_Segment9.Segment_G
  N79: 7_Segment9.common_cathode, R18.Pin_0, R20.Pin_1
  N80: 7_Segment10.common_cathode, R17.Pin_0, R19.Pin_1
  N81: 7_Segment11.Segment_E, R22.Pin_1, Componente5.5V
  N82: 7_Segment11.common_cathode, R21.Pin_0
  N83: 7_Segment12.Segment_E, R21.Pin_1, Componente5.GND
  N84: 7_Segment12.common_cathode, R22.Pin_0

notes:
  Conexión en cascada de ctos. 74HC595 y Displays de 7 segmentos (Cátodo Común) - NANO
  Conexión en cascada de ctos. 74HC595 y Displays de 7 segmentos (Ánodo Común) - NANO
  Conexión en cascada de ctos. 74HC595 y Displays de 7 segmentos (Cátodo Común) - UNO
  Para determinar si un display es de Ánodo o Cátodo común:
  Si al conectar el esquema de la izquierda enciende el segmento, el dispaly es de Cátodo Común
  Si al conectar el esquema de la derecha enciende el segmento, el dispaly es de Ánodo Común
